// Logisim project compare-master.circ as structural Verilog: 2 circuits, main circuit main
module main (
  output [3:0] X,
  output [3:0] Y,
  output halt,
  output \output 
);

  wire clock_1_out;

  Clock clock_1 (.out(clock_1_out));
  Counter counter_1 (.Q({Y, X}), .carry(halt), .clk(clock_1_out));  // open: load, D, count, clr
  sample sample_1 (.X(X), .Y(Y), .out_3(\output ));
endmodule

// compare-master
module sample (
  input  [3:0] X,
  input  [3:0] Y,
  output out_3
);

  Comparator #(.width(4)) comparator_1 (.a(X), .b(Y), .eq(out_3));  // open: gt, lt
endmodule
